// Logisim project Assignment1.circ as structural Verilog: 9 circuits, main circuit main
module main (
  input  SetTime,
  input  SetAlarm,
  input  EnableAlarm
);

  wire and_1_out, and_2_out, and_3_out, and_4_out, and_5_out, and_6_out, and_7_out, and_8_out, and_9_out,
       button_1_out, button_2_out, clock_1_out, d_ff_1_q, d_ff_2_qn, d_ff_3_q, d_ff_4_q, d_ff_5_q, d_ff_6_q,
       d_ff_7_q, hour_1_o1, hour_1_o2, hour_1_o3, hour_1_o4, hour_1_o5, hour_1_pm, minute_1_o1, minute_1_o2,
       minute_1_o3, minute_1_o4, minute_1_o5, minute_1_o7, minute_1_o8, minute_1_reset, not_1_out, not_2_out,
       or_1_out, or_2_out, or_3_out, or_4_out, register8bit_1_o1, register8bit_1_o2, register8bit_1_o3,
       register8bit_1_o4, register8bit_1_o5, register8bit_1_o6, register8bit_2_o1, register8bit_2_o2,
       register8bit_2_o3, register8bit_2_o4, register8bit_2_o5, register8bit_2_o6, register8bit_2_o7,
       register8bit_3_o1, register8bit_3_o2, register8bit_3_o3, register8bit_3_o4, register8bit_3_o5,
       register8bit_3_o6, register8bit_3_o7, register8bit_4_o1, register8bit_4_o2, register8bit_4_o3,
       register8bit_4_o4, register8bit_4_o5, register8bit_4_o6, register8bit_6_o1, register8bit_6_o2,
       register8bit_6_o3, register8bit_6_o4, register8bit_6_o5, register8bit_6_o6, register8bitdown_1_o6,
       register8bitdown_2_o1, register8bitdown_2_o2, register8bitdown_2_o3, register8bitdown_2_o4,
       register8bitdown_2_o5, register8bitdown_2_o6, register8bitdown_2_o7, xnor_1_out, xnor_2_out,
       xnor_3_out, xnor_4_out, xnor_5_out, xnor_6_out, xnor_7_out, xnor_8_out, xnor_9_out, xnor_10_out,
       xnor_11_out, xnor_12_out, xnor_13_out;
  wire [0:0] register8bitdown_1_o5;
  wire [2:0] register8bit_5_o5;
  wire [3:0] register8bit_5_o1, register8bitdown_1_o1;

  Clock clock_1 (.out(clock_1_out));
  Button button_1 (.out(button_1_out));
  Button button_2 (.out(button_2_out));
  D_Flip_Flop #(.trigger("falling")) d_ff_1 (.D(1'b1), .Q(d_ff_1_q), .reset(d_ff_1_q));  // open: clk, Qn, preset
  not not_1 (not_1_out, or_1_out);
  or or_1 (or_1_out, SetTime, SetAlarm);
  and and_1 (and_1_out, clock_1_out, not_1_out);
  and and_2 (and_2_out, button_1_out, or_1_out);
  and and_3 (and_3_out, button_2_out, or_1_out);
  or or_2 (or_2_out, and_1_out, d_ff_1_q, and_2_out);
  D_Flip_Flop d_ff_2 (.D(1'b0), .clk(and_1_out), .Qn(d_ff_2_qn), .preset(SetAlarm));  // open: Q, reset
  D_Flip_Flop #(.trigger("falling")) d_ff_3 (
    .D(1'b1), .clk(SetAlarm), .Q(d_ff_3_q), .reset(d_ff_3_q));  // open: Qn, preset
  D_Flip_Flop d_ff_4 (.D(1'b0), .clk(and_2_out), .Q(d_ff_4_q), .preset(and_6_out), .reset(d_ff_6_q));  // open: Qn
  and and_4 (and_4_out, and_1_out, d_ff_6_q);
  or or_3 (or_3_out, d_ff_1_q, and_3_out, and_4_out);
  D_Flip_Flop #(.trigger("falling")) d_ff_5 (
    .D(1'b1), .clk(SetAlarm), .Q(d_ff_5_q), .reset(d_ff_5_q));  // open: Qn, preset
  D_Flip_Flop #(.trigger("falling")) d_ff_6 (.D(d_ff_4_q), .clk(or_4_out), .Q(d_ff_6_q));  // open: Qn, preset, reset
  or or_4 (or_4_out, and_2_out, and_1_out);
  and and_5 (and_5_out, d_ff_2_qn, EnableAlarm);
  not not_2 (not_2_out, EnableAlarm);
  and and_6 (and_6_out, minute_1_reset, register8bit_5_o5[0], register8bit_5_o5[2]);
  Register8Bit register8bit_1 (
    .I4(hour_1_o4), .I5(hour_1_o5), .I6(hour_1_pm), .I1(hour_1_o1), .I2(hour_1_o2), .I3(hour_1_o3),
    .ClockInp(SetAlarm), .O4(register8bit_1_o4), .O5(register8bit_1_o5), .O6(register8bit_1_o6),
    .O1(register8bit_1_o1), .O2(register8bit_1_o2), .O3(register8bit_1_o3));  // open: S5, S6, S7, S8, S1, S2, S3, S4, Set, I7, I8, O7, O8
  Register8Bit register8bit_2 (
    .I4(minute_1_o4), .I5(minute_1_o5), .I6(minute_1_o7), .I7(minute_1_o8), .I1(minute_1_o1),
    .I2(minute_1_o2), .I3(minute_1_o3), .ClockInp(SetAlarm), .O4(register8bit_2_o4), .O5(register8bit_2_o5),
    .O6(register8bit_2_o6), .O7(register8bit_2_o7), .O1(register8bit_2_o1), .O2(register8bit_2_o2),
    .O3(register8bit_2_o3));  // open: S5, S6, S7, S8, S1, S2, S3, S4, Set, I8, O8
  Minute minute_1 (
    .S2(register8bit_2_o2), .S6(register8bit_2_o6), .S3(register8bit_2_o3), .S7(register8bit_2_o7),
    .S4(register8bit_2_o4), .ClockInp(or_2_out), .Set(d_ff_3_q), .S1(register8bit_2_o1),
    .S5(register8bit_2_o5), .O2(minute_1_o2), .O7(minute_1_o7), .O3(minute_1_o3), .O8(minute_1_o8),
    .O4(minute_1_o4), .Reset(minute_1_reset), .O1(minute_1_o1), .O5(minute_1_o5));  // open: SetTime, Add
  LED PM (.in(register8bitdown_1_o6));
  Hour hour_1 (
    .ClockInp(or_3_out), .Set(d_ff_5_q), .S5(register8bit_1_o5), .S1(register8bit_1_o1),
    .S2(register8bit_1_o2), .S3(register8bit_1_o3), .S4(register8bit_1_o4), .S6(register8bit_1_o6),
    .O1(hour_1_o1), .O5(hour_1_o5), .O2(hour_1_o2), .O3(hour_1_o3), .O4(hour_1_o4), .PM(hour_1_pm));  // open: SetTime, Add
  Hex_Digit_Display hex_digit_display_1 (.value({3'b000, register8bitdown_1_o5[0]}));  // open: dp
  Hex_Digit_Display hex_digit_display_2 (.value(register8bitdown_1_o1));  // open: dp
  Hex_Digit_Display hex_digit_display_3 (.value({1'b0, register8bit_5_o5}));  // open: dp
  Hex_Digit_Display hex_digit_display_4 (.value(register8bit_5_o1));  // open: dp
  LED Alarm (.in(d_ff_7_q));
  Register8Bit register8bit_3 (
    .I4(register8bit_5_o1[3]), .I5(register8bit_5_o5[0]), .I6(register8bit_5_o5[1]),
    .I7(register8bit_5_o5[2]), .I1(register8bit_5_o1[0]), .I2(register8bit_5_o1[1]),
    .I3(register8bit_5_o1[2]), .ClockInp(SetAlarm), .O4(register8bit_3_o4), .O5(register8bit_3_o5),
    .O6(register8bit_3_o6), .O7(register8bit_3_o7), .O1(register8bit_3_o1), .O2(register8bit_3_o2),
    .O3(register8bit_3_o3));  // open: S5, S6, S7, S8, S1, S2, S3, S4, Set, I8, O8
  Register8Bit register8bit_4 (
    .I4(register8bitdown_1_o1[3]), .I5(register8bitdown_1_o5[0]), .I6(register8bitdown_1_o6),
    .I1(register8bitdown_1_o1[0]), .I2(register8bitdown_1_o1[1]), .I3(register8bitdown_1_o1[2]),
    .ClockInp(SetAlarm), .O4(register8bit_4_o4), .O5(register8bit_4_o5), .O6(register8bit_4_o6),
    .O1(register8bit_4_o1), .O2(register8bit_4_o2), .O3(register8bit_4_o3));  // open: S5, S6, S7, S8, S1, S2, S3, S4, Set, I7, I8, O7, O8
  Register8Bit register8bit_5 (
    .S5(register8bit_3_o5), .S6(register8bit_3_o6), .S7(register8bit_3_o7), .S1(register8bit_3_o1),
    .S2(register8bit_3_o2), .S3(register8bit_3_o3), .S4(register8bit_3_o4), .Set(d_ff_3_q), .I4(minute_1_o4),
    .I5(minute_1_o5), .I6(minute_1_o7), .I7(minute_1_o8), .I1(minute_1_o1), .I2(minute_1_o2),
    .I3(minute_1_o3), .ClockInp(or_2_out), .O4(register8bit_5_o1[3]), .O5(register8bit_5_o5[0]),
    .O6(register8bit_5_o5[1]), .O7(register8bit_5_o5[2]), .O1(register8bit_5_o1[0]),
    .O2(register8bit_5_o1[1]), .O3(register8bit_5_o1[2]));  // open: S8, I8, O8
  Register8BitDown register8bitdown_1 (
    .S5(register8bit_4_o5), .S6(register8bit_4_o6), .S1(register8bit_4_o1), .S2(register8bit_4_o2),
    .S3(register8bit_4_o3), .S4(register8bit_4_o4), .Set(d_ff_5_q), .I4(hour_1_o4), .I5(hour_1_o5),
    .I6(hour_1_pm), .I1(hour_1_o1), .I2(hour_1_o2), .I3(hour_1_o3), .ClockInp(or_3_out),
    .O4(register8bitdown_1_o1[3]), .O5(register8bitdown_1_o5[0]), .O6(register8bitdown_1_o6),
    .O1(register8bitdown_1_o1[0]), .O2(register8bitdown_1_o1[1]), .O3(register8bitdown_1_o1[2]));  // open: S7, S8, I7, I8, O7, O8
  Register8Bit register8bit_6 (
    .I4(register8bitdown_1_o1[3]), .I5(register8bitdown_1_o5[0]), .I6(register8bitdown_1_o6),
    .I1(register8bitdown_1_o1[0]), .I2(register8bitdown_1_o1[1]), .I3(register8bitdown_1_o1[2]),
    .ClockInp(d_ff_5_q), .O4(register8bit_6_o4), .O5(register8bit_6_o5), .O6(register8bit_6_o6),
    .O1(register8bit_6_o1), .O2(register8bit_6_o2), .O3(register8bit_6_o3));  // open: S5, S6, S7, S8, S1, S2, S3, S4, Set, I7, I8, O7, O8
  Register8BitDown register8bitdown_2 (
    .I4(register8bit_5_o1[3]), .I5(register8bit_5_o5[0]), .I6(register8bit_5_o5[1]),
    .I7(register8bit_5_o5[2]), .I1(register8bit_5_o1[0]), .I2(register8bit_5_o1[1]),
    .I3(register8bit_5_o1[2]), .ClockInp(d_ff_3_q), .O4(register8bitdown_2_o4), .O5(register8bitdown_2_o5),
    .O6(register8bitdown_2_o6), .O7(register8bitdown_2_o7), .O1(register8bitdown_2_o1),
    .O2(register8bitdown_2_o2), .O3(register8bitdown_2_o3));  // open: S5, S6, S7, S8, S1, S2, S3, S4, Set, I8, O8
  xnor xnor_1 (xnor_1_out, register8bitdown_1_o1[0], register8bit_6_o1);
  xnor xnor_2 (xnor_2_out, register8bitdown_1_o1[1], register8bit_6_o2);
  xnor xnor_3 (xnor_3_out, register8bitdown_1_o1[2], register8bit_6_o3);
  xnor xnor_4 (xnor_4_out, register8bitdown_1_o1[3], register8bit_6_o4);
  xnor xnor_5 (xnor_5_out, register8bitdown_1_o5[0], register8bit_6_o5);
  xnor xnor_6 (xnor_6_out, register8bitdown_1_o6, register8bit_6_o6);
  xnor xnor_7 (xnor_7_out, register8bitdown_2_o1, register8bit_5_o1[0]);
  xnor xnor_8 (xnor_8_out, register8bitdown_2_o2, register8bit_5_o1[1]);
  xnor xnor_9 (xnor_9_out, register8bitdown_2_o3, register8bit_5_o1[2]);
  xnor xnor_10 (xnor_10_out, register8bitdown_2_o4, register8bit_5_o1[3]);
  xnor xnor_11 (xnor_11_out, register8bitdown_2_o5, register8bit_5_o5[0]);
  xnor xnor_12 (xnor_12_out, register8bitdown_2_o6, register8bit_5_o5[1]);
  xnor xnor_13 (xnor_13_out, register8bitdown_2_o7, register8bit_5_o5[2]);
  and and_7 (and_7_out, xnor_7_out, xnor_8_out, xnor_9_out, xnor_10_out, xnor_11_out, xnor_12_out, xnor_13_out);
  and and_8 (and_8_out, xnor_1_out, xnor_2_out, xnor_3_out, xnor_4_out, xnor_5_out, xnor_6_out);
  and and_9 (and_9_out, and_7_out, and_8_out, and_5_out);
  D_Flip_Flop d_ff_7 (.D(1'b0), .clk(not_2_out), .Q(d_ff_7_q), .preset(and_9_out));  // open: Qn, reset

  // Notes on the sheet:
  //   m+
  //   h+
  //   On: PM
  //   Off: AM
endmodule

module Minute (
  input  S1,
  input  S2,
  input  S3,
  input  S4,
  input  Set,
  input  ClockInp,
  input  SetTime,
  input  Add,
  input  S5,
  input  S6,
  input  S7,
  output O1,
  output O2,
  output O3,
  output O4,
  output Reset,
  output O5,
  output O7,
  output O8
);

  wire and_1_out, and_2_out, and_3_out, and_4_out, and_5_out, and_6_out, and_7_out, and_8_out, and_9_out,
       and_10_out, and_11_out, and_12_out, and_13_out, and_14_out, and_15_out, and_16_out, and_17_out,
       and_18_out, and_19_out, and_20_out, not_1_out, not_2_out, not_3_out, not_4_out, not_5_out, not_6_out,
       not_7_out, not_8_out, or_1_out, or_2_out, or_3_out, or_4_out, or_5_out, or_6_out, or_7_out, or_8_out;

  not not_1 (not_1_out, SetTime);
  and and_1 (and_1_out, ClockInp, not_1_out);
  and and_2 (and_2_out, SetTime, Add);
  not not_2 (not_2_out, S1);
  and and_3 (and_3_out, Set, not_2_out);
  or or_1 (or_1_out, and_1_out, and_2_out);
  and and_4 (and_4_out, Set, S1);
  J_K_Flip_Flop j_k_ff_1 (
    .J(1'b1), .K(1'b1), .clk(or_1_out), .Q(O1), .preset(and_4_out), .reset(or_2_out));  // open: Qn
  or or_2 (or_2_out, and_3_out, Reset);
  not not_3 (not_3_out, S5);
  and and_5 (and_5_out, Set, not_3_out);
  and and_6 (and_6_out, Set, S5);
  J_K_Flip_Flop j_k_ff_2 (.J(1'b1), .K(1'b1), .clk(Reset), .Q(O5), .preset(and_6_out), .reset(or_3_out));  // open: Qn
  or or_3 (or_3_out, and_5_out, and_19_out);
  not not_4 (not_4_out, S2);
  and and_7 (and_7_out, Set, not_4_out);
  and and_8 (and_8_out, Set, not_5_out);
  and and_9 (and_9_out, Set, S2);
  J_K_Flip_Flop j_k_ff_3 (.J(O1), .K(O1), .clk(or_1_out), .Q(O2), .preset(and_9_out), .reset(or_4_out));  // open: Qn
  or or_4 (or_4_out, and_7_out, Reset);
  not not_5 (not_5_out, S6);
  and and_10 (and_10_out, Set, S6);
  J_K_Flip_Flop j_k_ff_4 (.J(O5), .K(O5), .clk(Reset), .Q(O7), .preset(and_10_out), .reset(or_5_out));  // open: Qn
  or or_5 (or_5_out, and_8_out, and_19_out);
  not not_6 (not_6_out, S3);
  and and_11 (and_11_out, Set, not_6_out);
  and and_12 (and_12_out, O1, O2);
  and and_13 (and_13_out, Set, not_7_out);
  and and_14 (and_14_out, O5, O7);
  and and_15 (and_15_out, Set, S3);
  J_K_Flip_Flop j_k_ff_5 (
    .J(and_12_out), .K(and_12_out), .clk(or_1_out), .Q(O3), .preset(and_15_out), .reset(or_6_out));  // open: Qn
  or or_6 (or_6_out, and_11_out, Reset);
  not not_7 (not_7_out, S7);
  and and_16 (and_16_out, Set, S7);
  J_K_Flip_Flop j_k_ff_6 (
    .J(and_14_out), .K(and_14_out), .clk(Reset), .Q(O8), .preset(and_16_out), .reset(or_7_out));  // open: Qn
  or or_7 (or_7_out, and_13_out, and_19_out);
  not not_8 (not_8_out, S4);
  and and_17 (and_17_out, Set, not_8_out);
  and and_18 (and_18_out, and_12_out, O3);
  and and_19 (and_19_out, O7, O8);
  and and_20 (and_20_out, Set, S4);
  J_K_Flip_Flop j_k_ff_7 (
    .J(and_18_out), .K(and_18_out), .clk(or_1_out), .Q(O4), .preset(and_20_out), .reset(or_8_out));  // open: Qn
  or or_8 (or_8_out, and_17_out, Reset);
  and and_21 (Reset, O4, O2);
endmodule

module Hour (
  input  S1,
  input  S2,
  input  S3,
  input  S4,
  input  Set,
  input  ClockInp,
  input  SetTime,
  input  Add,
  input  S6,
  input  S5,
  output O1,
  output O2,
  output O3,
  output O4,
  output PM,
  output O5
);

  wire and_1_out, and_2_out, and_3_out, and_4_out, and_5_out, and_6_out, and_7_out, and_8_out, and_9_out,
       and_10_out, and_11_out, and_12_out, and_13_out, and_14_out, and_15_out, and_16_out, and_17_out,
       and_18_out, and_19_out, not_1_out, not_2_out, not_3_out, not_4_out, not_5_out, not_6_out, not_7_out,
       or_1_out, or_2_out, or_3_out, or_4_out, or_5_out, or_6_out;

  and and_1 (and_1_out, ClockInp, not_1_out);
  not not_1 (not_1_out, SetTime);
  and and_2 (and_2_out, SetTime, Add);
  or or_1 (or_1_out, and_1_out, and_2_out);
  or or_2 (or_2_out, and_17_out, and_9_out);
  and and_3 (and_3_out, Set, not_3_out);
  not not_2 (not_2_out, S5);
  and and_4 (and_4_out, Set, not_2_out);
  not not_3 (not_3_out, S1);
  and and_5 (and_5_out, Set, S1);
  J_K_Flip_Flop j_k_ff_1 (
    .J(1'b1), .K(1'b1), .clk(or_1_out), .Q(O1), .preset(and_5_out), .reset(or_3_out));  // open: Qn
  or or_3 (or_3_out, and_3_out, and_17_out);
  and and_6 (and_6_out, Set, S5);
  J_K_Flip_Flop j_k_ff_2 (
    .J(1'b1), .K(1'b1), .clk(or_2_out), .Q(O5), .preset(and_6_out), .reset(and_4_out));  // open: Qn
  not not_4 (not_4_out, S2);
  and and_7 (and_7_out, Set, not_4_out);
  and and_8 (and_8_out, Set, S2);
  J_K_Flip_Flop j_k_ff_3 (.J(O1), .K(O1), .clk(or_1_out), .Q(O2), .preset(and_8_out), .reset(or_4_out));  // open: Qn
  or or_4 (or_4_out, and_7_out, and_17_out, and_9_out);
  and and_9 (and_9_out, O1, O5, O2);
  not not_5 (not_5_out, S3);
  and and_10 (and_10_out, Set, not_5_out);
  and and_11 (and_11_out, O1, O2);
  and and_12 (and_12_out, Set, S3);
  J_K_Flip_Flop j_k_ff_4 (
    .J(and_11_out), .K(and_11_out), .clk(or_1_out), .Q(O3), .preset(and_12_out), .reset(or_5_out));  // open: Qn
  or or_5 (or_5_out, and_10_out, and_17_out);
  not not_6 (not_6_out, S4);
  and and_13 (and_13_out, Set, not_6_out);
  and and_14 (and_14_out, and_11_out, O3);
  and and_15 (and_15_out, Set, S4);
  J_K_Flip_Flop j_k_ff_5 (
    .J(and_14_out), .K(and_14_out), .clk(or_1_out), .Q(O4), .preset(and_15_out), .reset(or_6_out));  // open: Qn
  or or_6 (or_6_out, and_13_out, and_17_out);
  and and_16 (and_16_out, O2, O5);
  and and_17 (and_17_out, O4, O2);
  not not_7 (not_7_out, S6);
  and and_18 (and_18_out, Set, not_7_out);
  J_K_Flip_Flop j_k_ff_6 (
    .J(1'b1), .K(1'b1), .clk(and_16_out), .Q(PM), .preset(and_19_out), .reset(and_18_out));  // open: Qn
  and and_19 (and_19_out, Set, S6);
endmodule

module Register8Bit (
  input  S1,
  input  Set,
  input  ClockInp,
  input  I1,
  input  S2,
  input  I2,
  input  S3,
  input  I3,
  input  S4,
  input  I4,
  input  S5,
  input  I5,
  input  S6,
  input  I6,
  input  S7,
  input  I7,
  input  S8,
  input  I8,
  output O1,
  output O2,
  output O3,
  output O4,
  output O5,
  output O6,
  output O7,
  output O8
);

  wire and_1_out, and_2_out, and_3_out, and_4_out, and_5_out, and_6_out, and_7_out, and_8_out, and_9_out,
       and_10_out, and_11_out, and_12_out, and_13_out, and_14_out, and_15_out, and_16_out, not_1_out,
       not_2_out, not_3_out, not_4_out, not_5_out, not_6_out, not_7_out, not_8_out;

  and and_1 (and_1_out, Set, S1);
  D_Flip_Flop d_ff_1 (.D(I1), .clk(ClockInp), .Q(O1), .preset(and_1_out), .reset(and_9_out));  // open: Qn
  and and_2 (and_2_out, Set, S2);
  D_Flip_Flop d_ff_2 (.D(I2), .clk(ClockInp), .Q(O2), .preset(and_2_out), .reset(and_10_out));  // open: Qn
  and and_3 (and_3_out, Set, S3);
  D_Flip_Flop d_ff_3 (.D(I3), .clk(ClockInp), .Q(O3), .preset(and_3_out), .reset(and_11_out));  // open: Qn
  and and_4 (and_4_out, Set, S4);
  D_Flip_Flop d_ff_4 (.D(I4), .clk(ClockInp), .Q(O4), .preset(and_4_out), .reset(and_12_out));  // open: Qn
  and and_5 (and_5_out, Set, S5);
  D_Flip_Flop d_ff_5 (.D(I5), .clk(ClockInp), .Q(O5), .preset(and_5_out), .reset(and_13_out));  // open: Qn
  and and_6 (and_6_out, Set, S6);
  D_Flip_Flop d_ff_6 (.D(I6), .clk(ClockInp), .Q(O6), .preset(and_6_out), .reset(and_14_out));  // open: Qn
  and and_7 (and_7_out, Set, S7);
  D_Flip_Flop d_ff_7 (.D(I7), .clk(ClockInp), .Q(O7), .preset(and_7_out), .reset(and_15_out));  // open: Qn
  and and_8 (and_8_out, Set, S8);
  D_Flip_Flop d_ff_8 (.D(I8), .clk(ClockInp), .Q(O8), .preset(and_8_out), .reset(and_16_out));  // open: Qn
  not not_1 (not_1_out, S1);
  and and_9 (and_9_out, Set, not_1_out);
  not not_2 (not_2_out, S2);
  and and_10 (and_10_out, Set, not_2_out);
  not not_3 (not_3_out, S3);
  and and_11 (and_11_out, Set, not_3_out);
  not not_4 (not_4_out, S4);
  and and_12 (and_12_out, Set, not_4_out);
  not not_5 (not_5_out, S5);
  and and_13 (and_13_out, Set, not_5_out);
  not not_6 (not_6_out, S6);
  and and_14 (and_14_out, Set, not_6_out);
  not not_7 (not_7_out, S7);
  and and_15 (and_15_out, Set, not_7_out);
  not not_8 (not_8_out, S8);
  and and_16 (and_16_out, Set, not_8_out);
endmodule

module Register8BitDown (
  input  S1,
  input  Set,
  input  ClockInp,
  input  I1,
  input  S2,
  input  I2,
  input  S3,
  input  I3,
  input  S4,
  input  I4,
  input  S5,
  input  I5,
  input  S6,
  input  I6,
  input  S7,
  input  I7,
  input  S8,
  input  I8,
  output O1,
  output O2,
  output O3,
  output O4,
  output O5,
  output O6,
  output O7,
  output O8
);

  wire and_1_out, and_2_out, and_3_out, and_4_out, and_5_out, and_6_out, and_7_out, and_8_out, and_9_out,
       and_10_out, and_11_out, and_12_out, and_13_out, and_14_out, and_15_out, and_16_out, not_1_out,
       not_2_out, not_3_out, not_4_out, not_5_out, not_6_out, not_7_out, not_8_out;

  and and_1 (and_1_out, Set, S1);
  D_Flip_Flop d_ff_1 (.D(I1), .clk(ClockInp), .Q(O1), .preset(and_1_out), .reset(and_9_out));  // open: Qn
  and and_2 (and_2_out, Set, S2);
  D_Flip_Flop d_ff_2 (.D(I2), .clk(ClockInp), .Q(O2), .preset(and_2_out), .reset(and_10_out));  // open: Qn
  and and_3 (and_3_out, Set, S3);
  D_Flip_Flop d_ff_3 (.D(I3), .clk(ClockInp), .Q(O3), .preset(and_3_out), .reset(and_11_out));  // open: Qn
  and and_4 (and_4_out, Set, S4);
  D_Flip_Flop d_ff_4 (.D(I4), .clk(ClockInp), .Q(O4), .preset(and_4_out), .reset(and_12_out));  // open: Qn
  and and_5 (and_5_out, Set, S5);
  D_Flip_Flop d_ff_5 (.D(I5), .clk(ClockInp), .Q(O5), .preset(and_5_out), .reset(and_13_out));  // open: Qn
  and and_6 (and_6_out, Set, S6);
  D_Flip_Flop d_ff_6 (.D(I6), .clk(ClockInp), .Q(O6), .preset(and_6_out), .reset(and_14_out));  // open: Qn
  and and_7 (and_7_out, Set, S7);
  D_Flip_Flop d_ff_7 (.D(I7), .clk(ClockInp), .Q(O7), .preset(and_7_out), .reset(and_15_out));  // open: Qn
  and and_8 (and_8_out, Set, S8);
  D_Flip_Flop d_ff_8 (.D(I8), .clk(ClockInp), .Q(O8), .preset(and_8_out), .reset(and_16_out));  // open: Qn
  not not_1 (not_1_out, S1);
  and and_9 (and_9_out, Set, not_1_out);
  not not_2 (not_2_out, S2);
  and and_10 (and_10_out, Set, not_2_out);
  not not_3 (not_3_out, S3);
  and and_11 (and_11_out, Set, not_3_out);
  not not_4 (not_4_out, S4);
  and and_12 (and_12_out, Set, not_4_out);
  not not_5 (not_5_out, S5);
  and and_13 (and_13_out, Set, not_5_out);
  not not_6 (not_6_out, S6);
  and and_14 (and_14_out, Set, not_6_out);
  not not_7 (not_7_out, S7);
  and and_15 (and_15_out, Set, not_7_out);
  not not_8 (not_8_out, S8);
  and and_16 (and_16_out, Set, not_8_out);
endmodule

module Stage1 (
);

  wire and_1_out, and_2_out, and_3_out, and_4_out, and_5_out, clock_1_out, d_ff_1_q, j_k_ff_1_q, j_k_ff_2_q,
       j_k_ff_3_q, j_k_ff_4_q, j_k_ff_5_q, j_k_ff_6_q, j_k_ff_7_q, or_1_out;
  wire [2:0] d_ff_3_q;
  wire [3:0] d_ff_2_q;

  Clock clock_1 (.out(clock_1_out));
  D_Flip_Flop #(.trigger("falling")) d_ff_1 (.D(1'b1), .Q(d_ff_1_q), .reset(d_ff_1_q));  // open: clk, Qn, preset
  or or_1 (or_1_out, d_ff_1_q, clock_1_out);
  J_K_Flip_Flop j_k_ff_1 (.J(1'b1), .K(1'b1), .clk(or_1_out), .Q(j_k_ff_1_q), .reset(and_5_out));  // open: Qn, preset
  D_Flip_Flop d_ff_2 (.D(j_k_ff_1_q), .clk(or_1_out), .Q(d_ff_2_q[0]));  // open: Qn, preset, reset
  J_K_Flip_Flop j_k_ff_2 (.J(1'b1), .K(1'b1), .clk(and_5_out), .Q(j_k_ff_2_q), .reset(and_4_out));  // open: Qn, preset
  J_K_Flip_Flop j_k_ff_3 (
    .J(j_k_ff_1_q), .K(j_k_ff_1_q), .clk(or_1_out), .Q(j_k_ff_3_q), .reset(and_5_out));  // open: Qn, preset
  D_Flip_Flop d_ff_3 (.D(j_k_ff_2_q), .clk(clock_1_out), .Q(d_ff_3_q[0]));  // open: Qn, preset, reset
  D_Flip_Flop d_ff_4 (.D(j_k_ff_3_q), .clk(or_1_out), .Q(d_ff_2_q[1]));  // open: Qn, preset, reset
  J_K_Flip_Flop j_k_ff_4 (
    .J(j_k_ff_2_q), .K(j_k_ff_2_q), .clk(and_5_out), .Q(j_k_ff_4_q), .reset(and_4_out));  // open: Qn, preset
  and and_1 (and_1_out, j_k_ff_1_q, j_k_ff_3_q);
  J_K_Flip_Flop j_k_ff_5 (
    .J(and_1_out), .K(and_1_out), .clk(or_1_out), .Q(j_k_ff_5_q), .reset(and_5_out));  // open: Qn, preset
  D_Flip_Flop d_ff_5 (.D(j_k_ff_4_q), .clk(clock_1_out), .Q(d_ff_3_q[1]));  // open: Qn, preset, reset
  D_Flip_Flop d_ff_6 (.D(j_k_ff_5_q), .clk(or_1_out), .Q(d_ff_2_q[2]));  // open: Qn, preset, reset
  and and_2 (and_2_out, j_k_ff_2_q, j_k_ff_4_q);
  J_K_Flip_Flop j_k_ff_6 (
    .J(and_2_out), .K(and_2_out), .clk(and_5_out), .Q(j_k_ff_6_q), .reset(and_4_out));  // open: Qn, preset
  and and_3 (and_3_out, and_1_out, j_k_ff_5_q);
  J_K_Flip_Flop j_k_ff_7 (
    .J(and_3_out), .K(and_3_out), .clk(or_1_out), .Q(j_k_ff_7_q), .reset(and_5_out));  // open: Qn, preset
  D_Flip_Flop d_ff_7 (.D(j_k_ff_6_q), .clk(clock_1_out), .Q(d_ff_3_q[2]));  // open: Qn, preset, reset
  D_Flip_Flop d_ff_8 (.D(j_k_ff_7_q), .clk(or_1_out), .Q(d_ff_2_q[3]));  // open: Qn, preset, reset
  and and_4 (and_4_out, j_k_ff_4_q, j_k_ff_6_q);
  and and_5 (and_5_out, j_k_ff_7_q, j_k_ff_3_q);
  Hex_Digit_Display hex_digit_display_1 (.value(d_ff_2_q));  // open: dp
  Hex_Digit_Display hex_digit_display_2 (.value({1'b0, d_ff_3_q}));  // open: dp
endmodule

module Stage2 (
  input  Set_Time
);

  wire and_1_out, and_2_out, and_3_out, and_4_out, and_5_out, and_6_out, and_7_out, button_1_out,
       clock_1_out, d_ff_1_q, j_k_ff_1_q, j_k_ff_2_q, j_k_ff_3_q, j_k_ff_4_q, j_k_ff_5_q, j_k_ff_6_q,
       j_k_ff_7_q, not_1_out, or_1_out, or_2_out;
  wire [2:0] d_ff_3_q;
  wire [3:0] d_ff_2_q;

  Clock clock_1 (.out(clock_1_out));
  Button button_1 (.out(button_1_out));
  and and_1 (and_1_out, clock_1_out, not_1_out);
  not not_1 (not_1_out, Set_Time);
  and and_2 (and_2_out, Set_Time, button_1_out);
  D_Flip_Flop #(.trigger("falling")) d_ff_1 (.D(1'b1), .Q(d_ff_1_q), .reset(d_ff_1_q));  // open: clk, Qn, preset
  or or_1 (or_1_out, and_1_out, and_2_out);
  or or_2 (or_2_out, d_ff_1_q, or_1_out);
  J_K_Flip_Flop j_k_ff_1 (.J(1'b1), .K(1'b1), .clk(or_2_out), .Q(j_k_ff_1_q), .reset(and_7_out));  // open: Qn, preset
  D_Flip_Flop d_ff_2 (.D(j_k_ff_1_q), .clk(or_2_out), .Q(d_ff_2_q[0]));  // open: Qn, preset, reset
  J_K_Flip_Flop j_k_ff_2 (.J(1'b1), .K(1'b1), .clk(and_7_out), .Q(j_k_ff_2_q), .reset(and_6_out));  // open: Qn, preset
  J_K_Flip_Flop j_k_ff_3 (
    .J(j_k_ff_1_q), .K(j_k_ff_1_q), .clk(or_2_out), .Q(j_k_ff_3_q), .reset(and_7_out));  // open: Qn, preset
  D_Flip_Flop d_ff_3 (.D(j_k_ff_2_q), .clk(or_1_out), .Q(d_ff_3_q[0]));  // open: Qn, preset, reset
  D_Flip_Flop d_ff_4 (.D(j_k_ff_3_q), .clk(or_2_out), .Q(d_ff_2_q[1]));  // open: Qn, preset, reset
  J_K_Flip_Flop j_k_ff_4 (
    .J(j_k_ff_2_q), .K(j_k_ff_2_q), .clk(and_7_out), .Q(j_k_ff_4_q), .reset(and_6_out));  // open: Qn, preset
  and and_3 (and_3_out, j_k_ff_1_q, j_k_ff_3_q);
  J_K_Flip_Flop j_k_ff_5 (
    .J(and_3_out), .K(and_3_out), .clk(or_2_out), .Q(j_k_ff_5_q), .reset(and_7_out));  // open: Qn, preset
  and and_4 (and_4_out, j_k_ff_2_q, j_k_ff_4_q);
  D_Flip_Flop d_ff_5 (.D(j_k_ff_4_q), .clk(or_1_out), .Q(d_ff_3_q[1]));  // open: Qn, preset, reset
  D_Flip_Flop d_ff_6 (.D(j_k_ff_5_q), .clk(or_2_out), .Q(d_ff_2_q[2]));  // open: Qn, preset, reset
  J_K_Flip_Flop j_k_ff_6 (
    .J(and_4_out), .K(and_4_out), .clk(and_7_out), .Q(j_k_ff_6_q), .reset(and_6_out));  // open: Qn, preset
  and and_5 (and_5_out, and_3_out, j_k_ff_5_q);
  J_K_Flip_Flop j_k_ff_7 (
    .J(and_5_out), .K(and_5_out), .clk(or_2_out), .Q(j_k_ff_7_q), .reset(and_7_out));  // open: Qn, preset
  and and_6 (and_6_out, j_k_ff_4_q, j_k_ff_6_q);
  D_Flip_Flop d_ff_7 (.D(j_k_ff_6_q), .clk(or_1_out), .Q(d_ff_3_q[2]));  // open: Qn, preset, reset
  D_Flip_Flop d_ff_8 (.D(j_k_ff_7_q), .clk(or_2_out), .Q(d_ff_2_q[3]));  // open: Qn, preset, reset
  and and_7 (and_7_out, j_k_ff_7_q, j_k_ff_3_q);
  Hex_Digit_Display hex_digit_display_1 (.value(d_ff_2_q));  // open: dp
  Hex_Digit_Display hex_digit_display_2 (.value({1'b0, d_ff_3_q}));  // open: dp

  // Notes on the sheet:
  //   m+
endmodule

module Stage3 (
  input  Set_Time
);

  wire and_1_out, and_2_out, and_3_out, and_4_out, and_5_out, and_6_out, and_7_out, button_1_out,
       clock_1_out, d_ff_1_q, d_ff_6_q, j_k_ff_1_q, j_k_ff_2_q, j_k_ff_3_q, j_k_ff_4_q, j_k_ff_5_q,
       j_k_ff_6_q, not_1_out, or_1_out, or_2_out, or_3_out, or_4_out, undriven;
  wire [0:0] d_ff_3_q;
  wire [3:0] d_ff_2_q;

  Clock clock_1 (.out(clock_1_out));
  Button button_1 (.out(button_1_out));
  and and_1 (and_1_out, clock_1_out, not_1_out);
  not not_1 (not_1_out, Set_Time);
  and and_2 (and_2_out, Set_Time, button_1_out);
  D_Flip_Flop #(.trigger("falling")) d_ff_1 (.D(1'b1), .Q(d_ff_1_q), .reset(d_ff_1_q));  // open: clk, Qn, preset
  or or_1 (or_1_out, and_1_out, and_2_out);
  or or_2 (or_2_out, and_7_out, and_3_out);
  or or_3 (or_3_out, d_ff_1_q, or_1_out);
  J_K_Flip_Flop j_k_ff_1 (.J(1'b1), .K(1'b1), .clk(or_3_out), .Q(j_k_ff_1_q), .reset(and_7_out));  // open: Qn, preset
  J_K_Flip_Flop j_k_ff_2 (.J(1'b1), .K(1'b1), .clk(or_2_out), .Q(j_k_ff_2_q), .reset(undriven));  // open: Qn, preset
  D_Flip_Flop d_ff_2 (.D(j_k_ff_1_q), .clk(or_3_out), .Q(d_ff_2_q[0]));  // open: Qn, preset, reset
  D_Flip_Flop d_ff_3 (.D(j_k_ff_2_q), .clk(or_1_out), .Q(d_ff_3_q[0]));  // open: Qn, preset, reset
  J_K_Flip_Flop j_k_ff_3 (
    .J(j_k_ff_1_q), .K(j_k_ff_1_q), .clk(or_3_out), .Q(j_k_ff_3_q), .reset(or_4_out));  // open: Qn, preset
  or or_4 (or_4_out, and_7_out, and_3_out);
  and and_3 (and_3_out, j_k_ff_1_q, j_k_ff_2_q, j_k_ff_3_q);
  D_Flip_Flop d_ff_4 (.D(j_k_ff_3_q), .clk(or_3_out), .Q(d_ff_2_q[1]));  // open: Qn, preset, reset
  and and_4 (and_4_out, j_k_ff_1_q, j_k_ff_3_q);
  J_K_Flip_Flop j_k_ff_4 (
    .J(and_4_out), .K(and_4_out), .clk(or_3_out), .Q(j_k_ff_4_q), .reset(and_7_out));  // open: Qn, preset
  J_K_Flip_Flop j_k_ff_5 (.J(1'b1), .K(1'b1), .clk(and_5_out), .Q(j_k_ff_5_q));  // open: Qn, preset, reset
  and and_5 (and_5_out, j_k_ff_3_q, j_k_ff_2_q);
  D_Flip_Flop d_ff_5 (.D(j_k_ff_4_q), .clk(or_3_out), .Q(d_ff_2_q[2]));  // open: Qn, preset, reset
  D_Flip_Flop d_ff_6 (.D(j_k_ff_5_q), .clk(or_1_out), .Q(d_ff_6_q));  // open: Qn, preset, reset
  and and_6 (and_6_out, and_4_out, j_k_ff_4_q);
  J_K_Flip_Flop j_k_ff_6 (
    .J(and_6_out), .K(and_6_out), .clk(or_3_out), .Q(j_k_ff_6_q), .reset(and_7_out));  // open: Qn, preset
  D_Flip_Flop d_ff_7 (.D(j_k_ff_6_q), .clk(or_3_out), .Q(d_ff_2_q[3]));  // open: Qn, preset, reset
  and and_7 (and_7_out, j_k_ff_6_q, j_k_ff_3_q);
  Hex_Digit_Display hex_digit_display_1 (.value(d_ff_2_q));  // open: dp
  Hex_Digit_Display hex_digit_display_2 (.value({3'b000, d_ff_3_q[0]}));  // open: dp
  LED PM (.in(d_ff_6_q));

  // Notes on the sheet:
  //   h+
  //   On: PM
  //   Off: AM
endmodule

module Stage4 (
  input  SetTime
);

  wire and_1_out, and_2_out, and_3_out, and_4_out, and_5_out, button_1_out, button_2_out, clock_1_out,
       d_ff_1_q, d_ff_2_q, d_ff_3_q, hour_1_o1, hour_1_o2, hour_1_o3, hour_1_o4, hour_1_o5, hour_1_pm,
       minute_1_o1, minute_1_o2, minute_1_o3, minute_1_o4, minute_1_o5, minute_1_o7, minute_1_o8,
       minute_1_reset, not_1_out, or_1_out, or_2_out, or_3_out, register8bitdown_1_o6;
  wire [0:0] register8bitdown_1_o5;
  wire [2:0] register8bit_1_o5;
  wire [3:0] register8bit_1_o1, register8bitdown_1_o1;

  Clock clock_1 (.out(clock_1_out));
  Button button_1 (.out(button_1_out));
  Button button_2 (.out(button_2_out));
  D_Flip_Flop #(.trigger("falling")) d_ff_1 (.D(1'b1), .Q(d_ff_1_q), .reset(d_ff_1_q));  // open: clk, Qn, preset
  and and_1 (and_1_out, clock_1_out, not_1_out);
  not not_1 (not_1_out, SetTime);
  and and_2 (and_2_out, button_1_out, SetTime);
  and and_3 (and_3_out, button_2_out, SetTime);
  or or_1 (or_1_out, and_1_out, d_ff_1_q, and_2_out);
  D_Flip_Flop d_ff_2 (.Q(d_ff_2_q), .preset(and_5_out), .reset(d_ff_3_q));  // open: D, clk, Qn
  and and_4 (and_4_out, and_1_out, d_ff_3_q);
  or or_2 (or_2_out, d_ff_1_q, and_3_out, and_4_out);
  and and_5 (and_5_out, minute_1_reset, register8bit_1_o5[0], register8bit_1_o5[2]);
  D_Flip_Flop #(.trigger("falling")) d_ff_3 (.D(d_ff_2_q), .clk(or_3_out), .Q(d_ff_3_q));  // open: Qn, preset, reset
  or or_3 (or_3_out, and_2_out, and_1_out);
  Minute minute_1 (
    .ClockInp(or_1_out), .O2(minute_1_o2), .O7(minute_1_o7), .O3(minute_1_o3), .O8(minute_1_o8),
    .O4(minute_1_o4), .Reset(minute_1_reset), .O1(minute_1_o1), .O5(minute_1_o5));  // open: S2, S6, S3, S7, S4, SetTime, Add, Set, S1, S5
  Hour hour_1 (
    .ClockInp(or_2_out), .O1(hour_1_o1), .O5(hour_1_o5), .O2(hour_1_o2), .O3(hour_1_o3), .O4(hour_1_o4),
    .PM(hour_1_pm));  // open: SetTime, Add, Set, S5, S1, S2, S3, S4, S6
  Register8Bit register8bit_1 (
    .I4(minute_1_o4), .I5(minute_1_o5), .I6(minute_1_o7), .I7(minute_1_o8), .I1(minute_1_o1),
    .I2(minute_1_o2), .I3(minute_1_o3), .ClockInp(or_1_out), .O4(register8bit_1_o1[3]),
    .O5(register8bit_1_o5[0]), .O6(register8bit_1_o5[1]), .O7(register8bit_1_o5[2]),
    .O1(register8bit_1_o1[0]), .O2(register8bit_1_o1[1]), .O3(register8bit_1_o1[2]));  // open: S5, S6, S7, S8, S1, S2, S3, S4, Set, I8, O8
  Register8BitDown register8bitdown_1 (
    .I4(hour_1_o4), .I5(hour_1_o5), .I6(hour_1_pm), .I1(hour_1_o1), .I2(hour_1_o2), .I3(hour_1_o3),
    .ClockInp(or_2_out), .O4(register8bitdown_1_o1[3]), .O5(register8bitdown_1_o5[0]),
    .O6(register8bitdown_1_o6), .O1(register8bitdown_1_o1[0]), .O2(register8bitdown_1_o1[1]),
    .O3(register8bitdown_1_o1[2]));  // open: S5, S6, S7, S8, S1, S2, S3, S4, Set, I7, I8, O7, O8
  LED PM (.in(register8bitdown_1_o6));
  Hex_Digit_Display hex_digit_display_1 (.value({3'b000, register8bitdown_1_o5[0]}));  // open: dp
  Hex_Digit_Display hex_digit_display_2 (.value(register8bitdown_1_o1));  // open: dp
  Hex_Digit_Display hex_digit_display_3 (.value({1'b0, register8bit_1_o5}));  // open: dp
  Hex_Digit_Display hex_digit_display_4 (.value(register8bit_1_o1));  // open: dp

  // Notes on the sheet:
  //   m+
  //   h+
  //   On: PM
  //   Off: AM
endmodule
