// Logisim project LAB03.circ as structural Verilog: 1 circuit, main circuit main
module main (
  input  in_1,
  input  in_2,
  input  in_3,
  input  in_4,
  input  in_5,
  input  in_6,
  input  in_7
);

  wire and_1_out, and_2_out, clock_1_out, clock_2_out, d_ff_1_q, d_ff_2_q, d_ff_3_q, d_ff_4_q;
  wire [2:0] j_k_ff_1_q;

  Clock clock_1 (.out(clock_1_out));
  D_Flip_Flop d_ff_1 (.D(in_1), .clk(clock_1_out), .Q(d_ff_1_q), .reset(in_5));  // open: Qn, preset
  Clock clock_2 (.out(clock_2_out));
  LED led_1 (.in(d_ff_1_q));
  J_K_Flip_Flop j_k_ff_1 (
    .J(in_6), .K(in_6), .clk(clock_2_out), .Q(j_k_ff_1_q[0]), .reset(and_2_out));  // open: Qn, preset
  LED led_2 (.in(j_k_ff_1_q[0]));
  D_Flip_Flop d_ff_2 (.D(in_2), .clk(clock_1_out), .Q(d_ff_2_q), .reset(in_5));  // open: Qn, preset
  J_K_Flip_Flop j_k_ff_2 (
    .J(in_6), .K(in_6), .clk(clock_2_out), .Q(j_k_ff_1_q[1]), .reset(and_2_out));  // open: Qn, preset
  D_Flip_Flop d_ff_3 (.D(in_3), .clk(clock_1_out), .Q(d_ff_3_q), .reset(in_5));  // open: Qn, preset
  LED led_3 (.in(d_ff_2_q));
  and and_1 (and_1_out, in_6, j_k_ff_1_q[1]);
  LED led_4 (.in(j_k_ff_1_q[1]));
  LED led_5 (.in(d_ff_3_q));
  J_K_Flip_Flop j_k_ff_3 (
    .J(and_1_out), .K(and_1_out), .clk(clock_2_out), .Q(j_k_ff_1_q[2]), .reset(and_2_out));  // open: Qn, preset
  D_Flip_Flop d_ff_4 (.D(in_4), .clk(clock_1_out), .Q(d_ff_4_q), .reset(in_5));  // open: Qn, preset
  LED led_6 (.in(d_ff_4_q));
  LED led_7 (.in(j_k_ff_1_q[2]));
  and and_2 (and_2_out, j_k_ff_1_q[2], j_k_ff_1_q[1]);
  Hex_Digit_Display hex_digit_display_1 (.value({in_7, j_k_ff_1_q}));  // open: dp
endmodule
