// Logisim project assignment1.circ as structural Verilog: 1 circuit, main circuit main
module main (
);

  wire [3:0] undriven, undriven_2, undriven_3, undriven_4;

  Hex_Digit_Display hex_digit_display_1 (.value(undriven));  // open: dp
  Hex_Digit_Display hex_digit_display_2 (.value(undriven_2));  // open: dp
  Hex_Digit_Display hex_digit_display_3 (.value(undriven_3));  // open: dp
  Hex_Digit_Display hex_digit_display_4 (.value(undriven_4));  // open: dp
endmodule
