// Logisim project lab4.circ as structural Verilog: 1 circuit, main circuit main
module main (
  input  in_1,
  input  in_2,
  input  in_3,
  input  in_4,
  input  in_5,
  input  in_6
);

  wire and_1_out, and_2_out, and_3_out, and_4_out, and_5_out, and_6_out, and_7_out, and_8_out, and_9_out,
       and_10_out, and_11_out, and_12_out, clock_1_out, clock_2_out, d_ff_1_q, d_ff_2_q, d_ff_3_q, d_ff_4_q,
       d_ff_5_q, d_ff_6_q, d_ff_7_q, not_1_out, not_2_out, not_3_out, not_4_out, not_5_out, not_6_out,
       or_1_out, or_2_out, or_3_out, or_4_out, or_5_out, or_6_out, or_7_out;

  Clock clock_1 (.out(clock_1_out));
  Clock clock_2 (.out(clock_2_out));
  not not_1 (not_1_out, in_1);
  buf and_1 (and_1_out, in_1);  // AND_Gate
  and and_2 (and_2_out, not_1_out, in_3);
  or or_1 (or_1_out, in_4, in_5);
  not not_2 (not_2_out, in_6);
  not not_3 (not_3_out, in_1);
  or or_2 (or_2_out, and_1_out, and_2_out);
  D_Flip_Flop d_ff_1 (.D(or_2_out), .clk(clock_1_out), .Q(d_ff_1_q));  // open: Qn, preset, reset
  LED led_1 (.in(or_1_out));
  D_Flip_Flop d_ff_2 (.D(not_2_out), .clk(clock_2_out), .Q(d_ff_2_q));  // open: Qn, preset, reset
  buf and_3 (and_3_out, in_1);  // AND_Gate
  and and_4 (and_4_out, not_3_out, d_ff_1_q);
  LED led_2 (.in(d_ff_1_q));
  LED led_3 (.in(d_ff_2_q));
  or or_3 (or_3_out, and_3_out, and_4_out);
  D_Flip_Flop d_ff_3 (.D(or_3_out), .clk(clock_1_out), .Q(d_ff_3_q));  // open: Qn, preset, reset
  D_Flip_Flop d_ff_4 (.D(or_4_out), .clk(clock_2_out), .Q(d_ff_4_q));  // open: Qn, preset, reset
  not not_4 (not_4_out, in_1);
  LED led_4 (.in(d_ff_3_q));
  and and_5 (and_5_out, d_ff_2_q, in_6);
  LED led_5 (.in(d_ff_4_q));
  buf and_6 (and_6_out, in_1);  // AND_Gate
  and and_7 (and_7_out, not_4_out, d_ff_3_q);
  and and_8 (and_8_out, not_2_out, not_2_out);
  or or_4 (or_4_out, and_5_out, and_8_out);
  not not_5 (not_5_out, in_1);
  or or_5 (or_5_out, and_6_out, and_7_out);
  D_Flip_Flop d_ff_5 (.D(or_5_out), .clk(clock_1_out), .Q(d_ff_5_q));  // open: Qn, preset, reset
  buf and_9 (and_9_out, in_1);  // AND_Gate
  and and_10 (and_10_out, not_5_out, d_ff_5_q);
  LED led_6 (.in(d_ff_5_q));
  or or_6 (or_6_out, and_9_out, and_10_out);
  D_Flip_Flop d_ff_6 (.D(or_6_out), .clk(clock_1_out), .Q(d_ff_6_q));  // open: Qn, preset, reset
  not not_6 (not_6_out, in_1);
  LED led_7 (.in(d_ff_6_q));
  and and_11 (and_11_out, in_1, in_2);
  and and_12 (and_12_out, not_6_out, d_ff_6_q);
  or or_7 (or_7_out, and_11_out, and_12_out);
  D_Flip_Flop d_ff_7 (.D(or_7_out), .clk(clock_1_out), .Q(d_ff_7_q));  // open: Qn, preset, reset
  LED led_8 (.in(d_ff_7_q));
endmodule
